# Fritzing sketch streets_two_rotary_potenciometers (saved by Fritzing 0.9.6b)
breadboards: 1

parts:
  Part1 = Arduino Nano (Rev3.0)
  R1 = Rotary Potentiometer (Small) [maximum_resistance=100kΩ package=THT]
  R2 = Rotary Potentiometer (Small) [maximum_resistance=100kΩ package=THT]

nets:
  N1: Part1.GND, R1.leg1, R2.leg2
  N2: Part1.5V, R1.leg2, R2.leg1
  N3: Part1.A1, R2.wiper
  N4: Part1.A0, R1.wiper
